// Logisim project LED_flash.circ as structural Verilog: 1 circuit, main circuit main
module main (
);

  wire and_1_out, and_2_out, and_3_out, and_4_out, button_1_out, button_2_out, d_ff_1_q, d_ff_2_q, d_ff_2_qn,
       nand_1_out, nand_2_out, nand_3_out, nand_4_out, not_1_out, not_3_out, not_4_out, not_5_out, or_1_out,
       or_2_out, pull_resistor_1_node, pull_resistor_2_node, pull_resistor_3_node;

  Button button_1 (.out(button_1_out));
  Button button_2 (.out(button_2_out));
  Pull_Resistor #(.pull(1)) pull_resistor_1 (.node(pull_resistor_1_node));
  D_Flip_Flop d_ff_1 (
    .clk(button_1_out), .D(or_1_out), .Q(d_ff_1_q), .en(pull_resistor_1_node), .reset(button_2_out));  // open: Qn, preset
  D_Flip_Flop d_ff_2 (
    .clk(button_1_out), .D(or_2_out), .Q(d_ff_2_q), .Qn(d_ff_2_qn), .en(pull_resistor_1_node),
    .reset(button_2_out));  // open: preset
  LED led_1 (.in(d_ff_1_q));
  LED led_2 (.in(d_ff_2_q));
  nand nand_1 (nand_1_out, d_ff_1_q, not_3_out);
  not not_1 (not_1_out, pull_resistor_2_node);
  Pull_Resistor #(.pull(1)) pull_resistor_2 (.node(pull_resistor_2_node));
  not not_2 (pull_resistor_2_node, d_ff_2_q);
  nand nand_2 (nand_2_out, d_ff_1_q, nand_1_out);
  nand nand_3 (nand_3_out, nand_1_out, not_3_out);
  Pull_Resistor #(.pull(1)) pull_resistor_3 (.node(pull_resistor_3_node));
  nand nand_4 (nand_4_out, nand_2_out, nand_3_out);
  not not_3 (not_3_out, pull_resistor_3_node);
  not not_4 (not_4_out, not_1_out);
  not not_5 (not_5_out, not_1_out);
  and and_1 (and_1_out, nand_4_out, not_4_out);
  and and_2 (and_2_out, d_ff_1_q, not_1_out);
  and and_3 (and_3_out, d_ff_2_qn, not_5_out);
  and and_4 (and_4_out, not_3_out, not_1_out);
  or or_1 (or_1_out, and_1_out, and_2_out);
  or or_2 (or_2_out, and_3_out, and_4_out);
endmodule
